# Fritzing sketch PCBdesign (saved by Fritzing 0.9.3b)
circuit board: 9.22881cm x 7.08175cm
breadboards: 1

parts:
  Part1 = Adafruit I2S Mic - SPH0645 [part_number="Adafruit #3421"]
  Part2 = HC-SR501 Body Sensor Module
  Raspberry_Pi_1 = Raspberry Pi 3 [part_number=RPI-3-V1.2]

nets:
  N1: Part1.DATA, Raspberry_Pi_1.GIPO20
  N2: Part1.WS, Raspberry_Pi_1.GIPO19
  VCC: Part2.VCC, Raspberry_Pi_1.5V
  N3: Part2.OUT, Raspberry_Pi_1.GIPO5
  GND: Part2.GND, Raspberry_Pi_1.GND

notes:
  SmartMirror

custom parts:
  Adafruit I2S Mic - SPH0645: For many microcontrollers, adding audio input is easy with one of our analog microphone breakouts. But as you get to bigger and better microcontrollers and microcomputers, you'll find that you don't always have an analog input, or maybe you want to avoid the noise that can seep in with an analog mic system. Once you get past 8-bit micros, you will often find an I2S peripheral, that can take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
  HC-SR501 Body Sensor Module: Pyroelectric Infrared PIR Motion Sensor Detector Module
