# Fritzing sketch TuanMinhNguyen2 (saved by Fritzing 0.9.3b)
circuit board: 5.59257cm x 5.67208cm
breadboards: 1

parts:
  hc-sr1 = hc-sr04
  LED1 = smd LED [color="Red (633nm)" package="1206 [SMD]"]
  LED2 = LED - 5mm [color="Red (633nm)" package="5 mm [THT]"]
  Part1 = Arduino Uno (Rev3) - ICSP

nets:
  VCC: hc-sr1.VCC, Part1.5V
  N1: hc-sr1.Trig, Part1.D12/MISO
  N2: hc-sr1.Echo, Part1.D11_PWM/MOSI
  GND: hc-sr1.GND, LED1.cathode, LED2.cathode, Part1.GND
  N3: LED1.anode, Part1.D13/SCK
  N4: LED2.anode, Part1.D3_PWM

notes:
  Minh
